# Fritzing sketch schematics (saved by Fritzing 0.8.7b)

parts:
  Parte1 = Arduino Nano (Rev3.0)
  J1 = Basic Servo
  M1 = Stepper Motor - Bipolar
  J2 = Power Jack [package=power_jack_slot]
  U1 = Voltage Regulator - 5V [part_number=7805 package="TO220 [THT]"]
  A1 = A4988
  R1 = Resistor [tolerance=±5% resistance=220 package=THT]
  D2F1 = D2F-FL Omron Snap Action Limit Switch with Level
  D2F2 = D2F-FL Omron Snap Action Limit Switch with Level
  R2 = Resistor [tolerance=±5% resistance=220 package=THT]

nets:
  N1: Parte1.D2, A1.DIRECTION
  N2: Parte1.D3, A1.STEP
  N3: Parte1.D4, D2F2.NO, R2.Pin_0
  N4: Parte1.D5, R1.Pin_0, D2F1.NO
  N5: Parte1.D9, J1.pulse
  GND: Parte1.GND, J1.gnd, J2.GND, U1.GND, A1.GND#19
  5V: Parte1.5V, A1.VDD, D2F1.COM
  N6: M1.A, A1.2B
  N7: M1.C, A1.2A
  N8: M1.B, A1.1A
  N9: M1.D, A1.1B
  N10: J2.PWR, U1.input_voltage, A1.VMOT
  N11: A1.GND#13, R1.Pin_1, R2.Pin_1

notes:
  A4988
  7805
  Arduino Nano
  Limit Switch
  Stepper
  Power jack (12V)

custom parts:
  D2F-FL Omron Snap Action Limit Switch with Level: Snap action switch with stainless steel lever.
